# Fritzing sketch RW-Micro - Electrical Layout (saved by Fritzing 0.9.10b)

parts:
  Mod1 = ESP32 - CAM
  SERVO1 = Tower Pro SG90 servo [part_number=101246]
  SERVO2 = Tower Pro SG90 servo [part_number=101246]
  SERVO3 = Tower Pro SG90 servo [part_number=101246]
  USBTTL2 = USB TTL Serial Cable
  HC-SR04_Sensor_1 = HC-SR04 Ultrasonic Distance Sensor
  JP3 = Header 6 [package=1x06_smd_straight_alt]
  JP4 = Header 6 [package=1x06_smd_straight_alt]

nets:
  N1: Mod1.5V, JP3.1
  N2: Mod1.GND, Mod1.IO0, JP4.1
  N3: Mod1.IO12, SERVO1.Signal
  N4: Mod1.IO13, SERVO3.Signal
  N5: Mod1.IO15, SERVO2.Signal
  N6: Mod1.IO14, HC-SR04_Sensor_1.TRIG
  N7: Mod1.IO2, HC-SR04_Sensor_1.ECHO
  N8: Mod1.VOT, USBTTL2.RX
  N9: Mod1.VOR, USBTTL2.TX
  N10: SERVO1.+5V, JP3.5
  N11: SERVO1.GND, JP4.5
  N12: SERVO2.+5V, JP3.3
  N13: SERVO2.GND, JP4.3
  N14: SERVO3.+5V, JP3.4
  N15: SERVO3.GND, JP4.4
  N16: USBTTL2.5V, JP3.6
  N17: USBTTL2.GND, JP4.6
  N18: HC-SR04_Sensor_1.VCC, JP3.2
  N19: HC-SR04_Sensor_1.GND, JP4.2

notes:
  USB Plugs into Powerbank or Computer
  RED - 5V Power Rail
  BLACK - GND RAIL
  ESP32-CAM (AI Thinker)
  GPIO:12 = Left Servo
  GPIO:13 = Punch Servo
  GPIO:15 = Right Servo
  GPIO:14 = Trig (Ultrasonic)
  GPIO:02 = Echo (Ultrasonic)
  VOT = USB-TTL-RX
  VOR = USB-TTL-TX
  PINK - Only connected for programming
  GPIO:00 = GND

custom parts:
  ESP32 - CAM: The ESP32-CAM has a very competitive small-size camera module that can operate independently as a minimum system with a footprint of only 27*40.5*4.5mm and a deep sleep current of up to 6mA.
  Tower Pro SG90 servo: Original file by John De Cristofaro http://www.adafruit.com/products/1449 Adafruit Feedback Servo (Small) Edited by: e-radionica.com 28/9/2015
